# Fritzing sketch arduino-bluetooth-neopixels (saved by Fritzing 0.9.2b)

parts:
  Part1 = Arduino Uno (Rev3)
  RF1 = nRF8001 Bluetooth LE Breakout
  neopixel1 = Neopixel Ring 16
  CONN1 = USB connector [package=THT]
  R1 = Resistor [tolerance=±5% resistance=470 package=THT]
  U1 = POT [package=pot_alpha_rv16af-20]
  LED1 = smd LED [color="Blue (470nm)" package="0805 [SMD]"]
  R2 = Resistor [tolerance=±5% resistance=1k package=THT]

nets:
  N1: Part1.A0, U1.S
  N2: Part1.D9_PWM, RF1.RST
  N3: Part1.D10_PWM/SS, RF1.REQ
  N4: Part1.D11_PWM/MOSI, RF1.MOSI
  N5: Part1.D12/MISO, RF1.MISO
  N6: Part1.D13/SCK, RF1.SCK
  GND: Part1.GND, RF1.GND, neopixel1.GND, CONN1.GND, CONN1.chassis6, U1.E, LED1.cathode
  N7: Part1.D2, RF1.RDY
  N8: Part1.D3_PWM, R2.Pin_0
  N9: Part1.D6_PWM, R1.Pin_0
  5V: Part1.5V, RF1.VIN, U1.A
  VCC: neopixel1.VCC, CONN1.5V
  N10: neopixel1.IN, R1.Pin_1
  N11: LED1.anode, R2.Pin_1

custom parts:
  nRF8001 Bluetooth LE Breakout: nRF8001 Breakout Board
  Neopixel Ring 16: Neopixel Ring x16
